// Logisim project Single_cycle_block.circ as structural Verilog: 1 circuit, main circuit main
module main (
);

  wire clock_1_out, EXT_OP, less_falg, less_Unsign_falg, MEM_Read, MEM_Write, Reg_write, SSET, WB, Zero_flag;
  wire [1:0] ALU_SRC, PC_SELC, Rd_SRC;
  wire [3:0] func_4bit;
  wire [4:0] immd_L, multiplexer_1_out;
  wire [5:0] opcode;
  wire [9:0] block1_1_alu_op;
  wire [15:0] imm16;
  wire [15:11] main_3_instruction;
  wire [19:0] PC_Plus_1;
  wire [31:0] alu_1_alu_result, bit_extender_2_out, bit_extender_3_out, immdL_immdU, main_5_data_out,
       multiplexer_2_out, multiplexer_3_out, multiplexer_4_out, multiplexer_5_out, R0, R1, R2, R3, R4, R5,
       R6, R7, R8, R9, R10, R11, R12, R13, R14, R15, R16, R17, R18, R19, R20, R21, R22, R23, R24, R25, R26,
       R27, R28, R29, R30, R31, RS1, RS2, undriven;

  Clock clock_1 (.out(clock_1_out));
  PC_Control_Unit_main main_1 (
    .in_1(Zero_flag), .in_2(less_falg), .in_3(less_Unsign_falg), .op_code_5bit(opcode[4:0]), .out_5(PC_SELC));
  pc_new_main main_2 (
    .Pc_Selctor(PC_SELC), .Imm16({imm16[15:9], func_4bit, imm16[4:0]}), .RS1(RS1),
    .Immu({imm16[15:9], func_4bit}), .ImmL(immd_L), .PC_Output(PC_Plus_1), .Clk(clock_1_out));  // open: out_8
  main_control_unit main_control_unit_1 (
    .opcode(opcode), .reg_write(Reg_write), .sset(SSET), .ext_op(EXT_OP), .Rd_src(Rd_SRC), .alu_src(ALU_SRC),
    .mem_write(MEM_Write), .mem_read(MEM_Read), .wb(WB));
  Instruction_Mem_main main_3 (
    .Address(PC_Plus_1),
    .Instruction({imm16[15:9], func_4bit, imm16[4:0], main_3_instruction, immd_L, opcode}));
  assign immdL_immdU = {{16{imm16[15]}}, {imm16[15:9], func_4bit, immd_L}};  // Bit_Extender bit_extender_1
  assign bit_extender_2_out = {{16{imm16[15]}}, {imm16[15:9], func_4bit, imm16[4:0]}};  // Bit_Extender bit_extender_2
  assign bit_extender_3_out = {{16{1'b0}}, {imm16[15:9], func_4bit, imm16[4:0]}};  // Bit_Extender bit_extender_3
  Multiplexer #(.width(5), .enable("false")) multiplexer_1 (
    .in0(imm16[4:0]), .in1(immd_L), .out(multiplexer_1_out), .sel(SSET));
  Multiplexer #(.width(32), .enable("false")) multiplexer_2 (
    .in0(bit_extender_2_out), .in1(bit_extender_3_out), .out(multiplexer_2_out), .sel(EXT_OP));
  regfile_new_main main_4 (
    .Ra(main_3_instruction), .Rb(multiplexer_1_out), .Rw(immd_L), .Reg_write(Reg_write),
    .Bus_W(multiplexer_3_out), .Bus_A(RS1), .Bus_B(RS2), .Clk(clock_1_out), .R1(R1), .R2(R2), .R3(R3),
    .R4(R4), .R0(R0), .R5(R5), .R6(R6), .R7(R7), .R8(R8), .R9(R9), .R10(R10), .R11(R11), .R12(R12),
    .R13(R13), .R14(R14), .R15(R15), .R16(R16), .R17(R17), .R18(R18), .R19(R19), .R20(R20), .R21(R21),
    .R22(R22), .R23(R23), .R24(R24), .R25(R25), .R26(R26), .R27(R27), .R28(R28), .R29(R29), .R30(R30),
    .R31(R31));
  Multiplexer #(.select(2), .width(32), .enable("false")) multiplexer_3 (
    .in0({RS2[15:0], imm16[15:9], func_4bit, imm16[4:0]}), .in1(multiplexer_2_out), .in2(multiplexer_5_out),
    .in3(undriven), .out(multiplexer_3_out), .sel(Rd_SRC));
  Bit_Extender #(.in_width(32), .out_width(20)) bit_extender_4 (.in(undriven), .out(PC_Plus_1));
  Multiplexer #(.select(2), .width(32), .enable("false")) multiplexer_4 (
    .in0(multiplexer_2_out), .in1(RS2), .in2(immdL_immdU), .out(multiplexer_4_out), .sel(ALU_SRC));  // open: in3
  block1 block1_1 (.op_code(opcode), .ALU_OP(block1_1_alu_op), .func(func_4bit));
  ALU alu_1 (
    .ALU_Result(alu_1_alu_result), .less_flag_unsign(less_falg), .less_flag(less_Unsign_falg),
    .Zero_flag(Zero_flag), .A(RS1), .B(multiplexer_4_out), .ALU_Opration(block1_1_alu_op));  // open: Overflow
  Data_Mem_main main_5 (
    .Mem_Write(MEM_Write), .Mem_Read(MEM_Read), .Clk(clock_1_out), .Data_In(RS2), .Data_Out(main_5_data_out),
    .Alu_Result(alu_1_alu_result));
  Multiplexer #(.width(32), .enable("false")) multiplexer_5 (
    .in0(alu_1_alu_result), .in1(main_5_data_out), .out(multiplexer_5_out), .sel(WB));

  // Other names for the same wires on the sheet: imm16[8:5] = func_4bit; immd_U[10:0] = {imm16[15:9], func_4bit}

  // Notes on the sheet:
  //   op_code
  //   function
  //   0-> SSET
  //   01-> SET
  //   10->ALU_Result
  //   imm16
endmodule
